// Logisim project grf.circ as structural Verilog: 2 circuits, main circuit main
module main (
);

  grf GRF ();  // open: in_3, in_4, in_5, in_6, out_7, out_8, in_1, in_2
endmodule

module grf (
  input  in_1,
  input  in_2,
  input  [4:0] in_3,
  input  [4:0] in_4,
  input  [4:0] in_5,
  input  [31:0] in_6,
  output [31:0] out_7,
  output [31:0] out_8
);

  wire undriven, WE0, WE1, WE2, WE3, WE4, WE5, WE6, WE7, WE8, WE9, WE10, WE11, WE12, WE13, WE14, WE15, WE16,
       WE17, WE18, WE19, WE20, WE21, WE22, WE23, WE24, WE25, WE26, WE27, WE28, WE29, WE30, WE31;
  wire [31:0] _0, _1, _2, _3, _4, _5, _6, _7, _8, _9, _10, _11, _12, _13, _14, _15, _16, _17, _18, _19, _20,
       _21, _22, _23, _24, _25, _26, _27, _28, _29, _30, _31;

  Demultiplexer #(.select(5)) demultiplexer_1 (
    .out0(WE0), .out1(WE1), .out2(WE2), .out3(WE3), .out4(WE4), .out5(WE5), .out6(WE6), .out7(WE7),
    .out8(WE8), .out9(WE9), .out10(WE10), .out11(WE11), .out12(WE12), .out13(WE13), .out14(WE14),
    .out15(WE15), .out16(WE16), .out17(WE17), .out18(WE18), .out19(WE19), .out20(WE20), .out21(WE21),
    .out22(WE22), .out23(WE23), .out24(WE24), .out25(WE25), .out26(WE26), .out27(WE27), .out28(WE28),
    .out29(WE29), .out30(WE30), .out31(WE31), .in(in_2), .sel(in_5));  // open: en
  Register #(.width(32)) register_1 (.D({32{1'b0}}), .en(WE0), .Q(_0), .clk(in_1));  // open: clr
  Register #(.width(32)) register_2 (.D(in_6), .en(WE4), .Q(_4), .clk(in_1));  // open: clr
  Register #(.width(32)) register_3 (.D(in_6), .en(WE8), .Q(_8), .clk(in_1));  // open: clr
  Register #(.width(32)) register_4 (.D(in_6), .en(WE12), .Q(_12), .clk(in_1));  // open: clr
  Register #(.width(32)) register_5 (.D(in_6), .en(WE16), .Q(_16), .clk(in_1));  // open: clr
  Register #(.width(32)) register_6 (.D(in_6), .en(WE20), .Q(_20), .clk(in_1));  // open: clr
  Register #(.width(32)) register_7 (.D(in_6), .en(WE24), .Q(_24), .clk(in_1));  // open: clr
  Register #(.width(32)) register_8 (.D(in_6), .en(WE28), .Q(_28), .clk(in_1));  // open: clr
  Register #(.width(32)) register_9 (.D(in_6), .en(WE1), .Q(_1), .clk(in_1));  // open: clr
  Register #(.width(32)) register_10 (.D(in_6), .en(WE5), .Q(_5), .clk(in_1));  // open: clr
  Register #(.width(32)) register_11 (.D(in_6), .en(WE9), .Q(_9), .clk(in_1));  // open: clr
  Register #(.width(32)) register_12 (.D(in_6), .en(WE13), .Q(_13), .clk(in_1));  // open: clr
  Register #(.width(32)) register_13 (.D(in_6), .en(WE17), .Q(_17), .clk(in_1));  // open: clr
  Register #(.width(32)) register_14 (.D(in_6), .en(WE21), .Q(_21), .clk(in_1));  // open: clr
  Register #(.width(32)) register_15 (.D(in_6), .en(WE25), .Q(_25), .clk(in_1));  // open: clr
  Register #(.width(32)) register_16 (.D(in_6), .en(WE29), .Q(_29), .clk(in_1), .clr(undriven));
  Register #(.width(32)) register_17 (.D(in_6), .en(WE2), .Q(_2), .clk(in_1));  // open: clr
  Register #(.width(32)) register_18 (.D(in_6), .en(WE6), .Q(_6), .clk(in_1));  // open: clr
  Register #(.width(32)) register_19 (.D(in_6), .en(WE10), .Q(_10), .clk(in_1));  // open: clr
  Register #(.width(32)) register_20 (.D(in_6), .en(WE14), .Q(_14), .clk(in_1));  // open: clr
  Register #(.width(32)) register_21 (.D(in_6), .en(WE18), .Q(_18), .clk(in_1));  // open: clr
  Register #(.width(32)) register_22 (.D(in_6), .en(WE22), .Q(_22), .clk(in_1));  // open: clr
  Register #(.width(32)) register_23 (.D(in_6), .en(WE26), .Q(_26), .clk(in_1));  // open: clr
  Register #(.width(32)) register_24 (.D(in_6), .en(WE30), .Q(_30), .clk(in_1));  // open: clr
  Multiplexer #(.select(5), .width(32)) multiplexer_1 (
    .in0(_0), .in1(_1), .in2(_2), .in3(_3), .in4(_4), .in5(_5), .in6(_6), .in7(_7), .in8(_8), .in9(_9),
    .in10(_10), .in11(_11), .in12(_12), .in13(_13), .in14(_14), .in15(_15), .in16(_16), .in17(_17),
    .in18(_18), .in19(_19), .in20(_20), .in21(_21), .in22(_22), .in23(_23), .in24(_24), .in25(_25),
    .in26(_26), .in27(_27), .in28(_28), .in29(_29), .in30(_30), .in31(_31), .out(out_7), .sel(in_3));  // open: en
  Register #(.width(32)) register_25 (.D(in_6), .en(WE3), .Q(_3), .clk(in_1));  // open: clr
  Register #(.width(32)) register_26 (.D(in_6), .en(WE7), .Q(_7), .clk(in_1));  // open: clr
  Register #(.width(32)) register_27 (.D(in_6), .en(WE11), .Q(_11), .clk(in_1));  // open: clr
  Register #(.width(32)) register_28 (.D(in_6), .en(WE15), .Q(_15), .clk(in_1));  // open: clr
  Register #(.width(32)) register_29 (.D(in_6), .en(WE19), .Q(_19), .clk(in_1));  // open: clr
  Register #(.width(32)) register_30 (.D(in_6), .en(WE23), .Q(_23), .clk(in_1));  // open: clr
  Register #(.width(32)) register_31 (.D(in_6), .en(WE27), .Q(_27), .clk(in_1));  // open: clr
  Register #(.width(32)) register_32 (.D(in_6), .en(WE31), .Q(_31), .clk(in_1));  // open: clr
  Multiplexer #(.select(5), .width(32)) multiplexer_2 (
    .in0(_0), .in1(_1), .in2(_2), .in3(_3), .in4(_4), .in5(_5), .in6(_6), .in7(_7), .in8(_8), .in9(_9),
    .in10(_10), .in11(_11), .in12(_12), .in13(_13), .in14(_14), .in15(_15), .in16(_16), .in17(_17),
    .in18(_18), .in19(_19), .in20(_20), .in21(_21), .in22(_22), .in23(_23), .in24(_24), .in25(_25),
    .in26(_26), .in27(_27), .in28(_28), .in29(_29), .in30(_30), .in31(_31), .out(out_8), .sel(in_4));  // open: en

  // Other names for the same wires on the sheet: A1[4:0] = in_3; A2[4:0] = in_4; A3[4:0] = in_5; clk = in_1;
  //   RD1[31:0] = out_7; RD2[31:0] = out_8; WD[31:0] = in_6; WE = in_2
endmodule
