// Logisim project 单周期cpu钟.circ as structural Verilog: 7 circuits, main circuit main
module main (
  input  in_1,
  output [31:0] out_2,
  output out_3,
  output [4:0] out_4,
  output [31:0] out_5,
  output out_6,
  output [4:0] out_7,
  output [31:0] out_8
);

  wire alusrc, clk, extop, ifbeq, ifj, ifjal_writeaddress, ifjal_writedata, ifjr, memtoreg, regdst, zero;
  wire [1:0] aluop;
  wire [4:0] multiplexer_1_out;
  wire [31:0] alu_1_out_5, dm_1_out_6, ext_1_out_3, jr_rs, multiplexer_4_out, multiplexer_5_out, pc_4;

  Clock clock_1 (.out(clk));
  // Probe on out_2
  IFU ifu_1 (
    .ifbeq(ifbeq), .zero(zero), .ifj(ifj), .ifjr(ifjr), .jr_rs(jr_rs), .clk(clk), .reset(in_1),
    .instr(out_2), .pc_4(pc_4));
  Controller controller_1 (
    .opcode(out_2[31:26]), .func(out_2[5:0]), .ifbeq(ifbeq), .memwrite(out_6), .mentoreg(memtoreg),
    .alusrc(alusrc), .aluop(aluop), .regdst(regdst), .we(out_3), .extop(extop), .ifj(ifj),
    .ifjal_writeaddress(ifjal_writeaddress), .ifjr(ifjr), .ifjal_writedata(ifjal_writedata));
  Multiplexer #(.width(5)) multiplexer_1 (
    .in0(out_2[20:16]), .in1(out_2[15:11]), .out(multiplexer_1_out), .sel(regdst));  // open: en
  Multiplexer #(.width(5)) multiplexer_2 (
    .in0(multiplexer_1_out), .in1({5{1'b1}}), .out(out_4), .sel(ifjal_writeaddress));  // open: en
  GRF grf_1 (
    .A1(out_2[25:21]), .A2(out_2[20:16]), .A3(out_4), .WD(out_5), .clk(clk), .we(out_3), .reset(in_1),
    .RD1(jr_rs), .RD2(out_8));
  EXT ext_1 (.in_1(out_2[15:0]), .extop(extop), .out_3(ext_1_out_3));
  Multiplexer #(.width(32)) multiplexer_3 (
    .in0(multiplexer_5_out), .in1(pc_4), .out(out_5), .sel(ifjal_writedata));  // open: en
  Multiplexer #(.width(32)) multiplexer_4 (
    .in0(out_8), .in1(ext_1_out_3), .out(multiplexer_4_out), .sel(alusrc));  // open: en
  Multiplexer #(.width(32)) multiplexer_5 (
    .in0({alu_1_out_5[31:7], out_7, alu_1_out_5[1:0]}), .in1(dm_1_out_6), .out(multiplexer_5_out),
    .sel(memtoreg));  // open: en
  ALU alu_1 (
    .in_1(jr_rs), .in_3(multiplexer_4_out), .ALUop(aluop), .zero(zero),
    .out_5({alu_1_out_5[31:7], out_7, alu_1_out_5[1:0]}));
  DM dm_1 (.address(out_7), .write_data(out_8), .reset(in_1), .menwrite(out_6), .clk(clk), .out_6(dm_1_out_6));

  // Other names for the same wires on the sheet: menaddr[4:0] = out_7; imm16[15:0] = out_2[15:0]; instr[31:0] = out_2;
  //   rd[4:0] = out_2[15:11]; rt[4:0] = out_2[20:16]; rs[4:0] = out_2[25:21]; memdata[31:0] = out_8; memwrite = out_6;
  //   regaddr[4:0] = out_4; regdata[31:0] = out_5; reset = in_1; we = out_3
endmodule

// grf
module GRF (
  input  [4:0] A1,
  input  [4:0] A2,
  input  [4:0] A3,
  input  [31:0] WD,
  input  reset,
  input  clk,
  input  we,
  output [31:0] RD1,
  output [31:0] RD2
);

  wire we1, we2, we3, we4, we5, we6, we7, we8, we9, we10, we11, we12, we13, we14, we15, we16, we17, we18,
       we19, we20, we21, we22, we23, we24, we25, we26, we27, we28, we29, we30, we31;
  wire [31:0] in0, in1, in2, in3, in4, in5, in6, in7, in8, in9, in10, in11, in12, in13, in14, in15, in16,
       in17, in18, in19, in20, in21, in22, in23, in24, in25, in26, in27, in28, in29, in30, in31, out0, out1,
       out2, out3, out4, out5, out6, out7, out8, out9, out10, out11, out12, out13, out14, out15, out16,
       out17, out18, out19, out20, out21, out22, out23, out24, out25, out26, out27, out28, out29, out30,
       out31;

  Demultiplexer #(.select(5)) demultiplexer_1 (
    .out1(we1), .out2(we2), .out3(we3), .out4(we4), .out5(we5), .out6(we6), .out7(we7), .out8(we8),
    .out9(we9), .out10(we10), .out11(we11), .out12(we12), .out13(we13), .out14(we14), .out15(we15),
    .out16(we16), .out17(we17), .out18(we18), .out19(we19), .out20(we20), .out21(we21), .out22(we22),
    .out23(we23), .out24(we24), .out25(we25), .out26(we26), .out27(we27), .out28(we28), .out29(we29),
    .out30(we30), .out31(we31), .in(we), .sel(A3));  // open: out0, en
  Register #(.width(32)) _0 (.D(in0), .en(1'b0), .Q(out0), .clk(clk), .clr(reset));
  Register #(.width(32)) _1 (.D(in1), .en(we1), .Q(out1), .clk(clk), .clr(reset));
  Register #(.width(32)) _2 (.D(in2), .en(we2), .Q(out2), .clk(clk), .clr(reset));
  Register #(.width(32)) _3 (.D(in3), .en(we3), .Q(out3), .clk(clk), .clr(reset));
  Register #(.width(32)) _4 (.D(in4), .en(we4), .Q(out4), .clk(clk), .clr(reset));
  Register #(.width(32)) _5 (.D(in5), .en(we5), .Q(out5), .clk(clk), .clr(reset));
  Register #(.width(32)) _6 (.D(in6), .en(we6), .Q(out6), .clk(clk), .clr(reset));
  Register #(.width(32)) _7 (.D(in7), .en(we7), .Q(out7), .clk(clk), .clr(reset));
  Register #(.width(32)) _8 (.D(in8), .en(we8), .Q(out8), .clk(clk), .clr(reset));
  Register #(.width(32)) _9 (.D(in9), .en(we9), .Q(out9), .clk(clk), .clr(reset));
  Register #(.width(32)) _10 (.D(in10), .en(we10), .Q(out10), .clk(clk), .clr(reset));
  Register #(.width(32)) _11 (.D(in11), .en(we11), .Q(out11), .clk(clk), .clr(reset));
  Demultiplexer #(.select(5), .width(32)) demultiplexer_2 (
    .out0(in0), .out1(in1), .out2(in2), .out3(in3), .out4(in4), .out5(in5), .out6(in6), .out7(in7),
    .out8(in8), .out9(in9), .out10(in10), .out11(in11), .out12(in12), .out13(in13), .out14(in14),
    .out15(in15), .out16(in16), .out17(in17), .out18(in18), .out19(in19), .out20(in20), .out21(in21),
    .out22(in22), .out23(in23), .out24(in24), .out25(in25), .out26(in26), .out27(in27), .out28(in28),
    .out29(in29), .out30(in30), .out31(in31), .in(WD), .sel(A3));  // open: en
  Register #(.width(32)) _12 (.D(in12), .en(we12), .Q(out12), .clk(clk), .clr(reset));
  Register #(.width(32)) _13 (.D(in13), .en(we13), .Q(out13), .clk(clk), .clr(reset));
  Register #(.width(32)) _14 (.D(in14), .en(we14), .Q(out14), .clk(clk), .clr(reset));
  Register #(.width(32)) _15 (.D(in15), .en(we15), .Q(out15), .clk(clk), .clr(reset));
  Register #(.width(32)) _16 (.D(in16), .en(we16), .Q(out16), .clk(clk), .clr(reset));
  Register #(.width(32)) _17 (.D(in17), .en(we17), .Q(out17), .clk(clk), .clr(reset));
  Register #(.width(32)) _18 (.D(in18), .en(we18), .Q(out18), .clk(clk), .clr(reset));
  Register #(.width(32)) _19 (.D(in19), .en(we19), .Q(out19), .clk(clk), .clr(reset));
  Register #(.width(32)) _20 (.D(in20), .en(we20), .Q(out20), .clk(clk), .clr(reset));
  Register #(.width(32)) _21 (.D(in21), .en(we21), .Q(out21), .clk(clk), .clr(reset));
  Register #(.width(32)) _22 (.D(in22), .en(we22), .Q(out22), .clk(clk), .clr(reset));
  Register #(.width(32)) _23 (.D(in23), .en(we23), .Q(out23), .clk(clk), .clr(reset));
  Register #(.width(32)) _24 (.D(in24), .en(we24), .Q(out24), .clk(clk), .clr(reset));
  Register #(.width(32)) _25 (.D(in25), .en(we25), .Q(out25), .clk(clk), .clr(reset));
  Register #(.width(32)) _26 (.D(in26), .en(we26), .Q(out26), .clk(clk), .clr(reset));
  Register #(.width(32)) _27 (.D(in27), .en(we27), .Q(out27), .clk(clk), .clr(reset));
  Register #(.width(32)) _28 (.D(in28), .en(we28), .Q(out28), .clk(clk), .clr(reset));
  Register #(.width(32)) _29 (.D(in29), .en(we29), .Q(out29), .clk(clk), .clr(reset));
  Multiplexer #(.select(5), .width(32)) multiplexer_1 (
    .in0(out0), .in1(out1), .in2(out2), .in3(out3), .in4(out4), .in5(out5), .in6(out6), .in7(out7),
    .in8(out8), .in9(out9), .in10(out10), .in11(out11), .in12(out12), .in13(out13), .in14(out14),
    .in15(out15), .in16(out16), .in17(out17), .in18(out18), .in19(out19), .in20(out20), .in21(out21),
    .in22(out22), .in23(out23), .in24(out24), .in25(out25), .in26(out26), .in27(out27), .in28(out28),
    .in29(out29), .in30(out30), .in31(out31), .out(RD1), .sel(A1));  // open: en
  Register #(.width(32)) _30 (.D(in30), .en(we30), .Q(out30), .clk(clk), .clr(reset));
  Register #(.width(32)) _31 (.D(in31), .en(we31), .Q(out31), .clk(clk), .clr(reset));
  Multiplexer #(.select(5), .width(32)) multiplexer_2 (
    .in0(out0), .in1(out1), .in2(out2), .in3(out3), .in4(out4), .in5(out5), .in6(out6), .in7(out7),
    .in8(out8), .in9(out9), .in10(out10), .in11(out11), .in12(out12), .in13(out13), .in14(out14),
    .in15(out15), .in16(out16), .in17(out17), .in18(out18), .in19(out19), .in20(out20), .in21(out21),
    .in22(out22), .in23(out23), .in24(out24), .in25(out25), .in26(out26), .in27(out27), .in28(out28),
    .in29(out29), .in30(out30), .in31(out31), .out(RD2), .sel(A2));  // open: en
endmodule

// dm
module DM (
  input  [4:0] address,
  input  [31:0] write_data,
  input  reset,
  input  menwrite,
  input  clk,
  output [31:0] out_6
);

  RAM #(.addrWidth(5), .dataWidth(32), .bus("separate")) ram_1 (
    .addr(address), .din(write_data), .data(out_6), .str(menwrite), .clk(clk), .clr(reset));  // open: sel, ld
endmodule

// alu
module ALU (
  input  [31:0] in_1,
  input  [1:0] ALUop,
  input  [31:0] in_3,
  output zero,
  output [31:0] out_5
);

  wire comparator_1_eq;
  wire [31:0] adder_1_out, bit_extender_1_out, or_1_out, subtractor_1_out;

  Adder #(.width(32)) adder_1 (.a(in_1), .b(in_3), .out(adder_1_out));  // open: cin, cout
  Subtractor #(.width(32)) subtractor_1 (.a(in_1), .b(in_3), .out(subtractor_1_out));  // open: bin, bout
  assign or_1_out = in_1 | in_3;  // OR_Gate or_1, 32 bits wide
  Comparator #(.width(32)) comparator_1 (.a(in_1), .b(in_3), .eq(comparator_1_eq));  // open: gt, lt
  assign bit_extender_1_out = {{31{1'b0}}, comparator_1_eq};  // Bit_Extender bit_extender_1
  Comparator #(.width(32)) comparator_2 (.a(subtractor_1_out), .b({32{1'b0}}), .eq(zero));  // open: gt, lt
  Multiplexer #(.select(2), .width(32)) multiplexer_1 (
    .in0(adder_1_out), .in1(subtractor_1_out), .in2(or_1_out), .in3(bit_extender_1_out), .out(out_5),
    .sel(ALUop));  // open: en
endmodule

// controler
module Controller (
  input  [5:0] opcode,
  input  [5:0] func,
  output ifbeq,
  output memwrite,
  output mentoreg,
  output alusrc,
  output [1:0] aluop,
  output regdst,
  output we,
  output extop,
  output ifj,
  output ifjal_writeaddress,
  output ifjr,
  output ifjal_writedata
);

  wire addu, beq, j, jal, jalr, jr, lui, lw, not_1_out, not_2_out, not_3_out, not_4_out, not_5_out,
       not_6_out, not_7_out, not_8_out, not_9_out, not_10_out, not_11_out, not_12_out, sw;

  not not_1 (not_1_out, opcode[1]);
  not not_2 (not_2_out, opcode[0]);
  not not_3 (not_3_out, opcode[4]);
  not not_4 (not_4_out, opcode[3]);
  not not_5 (not_5_out, opcode[2]);
  not not_6 (not_6_out, opcode[5]);
  not not_7 (not_7_out, func[3]);
  not not_8 (not_8_out, func[0]);
  not not_9 (not_9_out, func[2]);
  not not_10 (not_10_out, func[1]);
  not not_11 (not_11_out, func[5]);
  not not_12 (not_12_out, func[4]);
  and u_addu (addu, not_2_out, not_1_out, not_5_out, not_4_out, not_3_out, not_6_out, func[0], not_10_out, not_9_out, not_7_out, not_12_out, func[5]);
  and subu (aluop[0], not_2_out, not_1_out, not_5_out, not_4_out, not_3_out, not_6_out, func[0], func[1], not_9_out, not_7_out, not_12_out, func[5]);
  and u_sw (sw, opcode[0], opcode[1], not_5_out, opcode[3], not_3_out, opcode[5]);
  and u_lw (lw, opcode[0], opcode[1], not_5_out, not_4_out, not_3_out, opcode[5]);
  and ori (aluop[1], opcode[0], not_1_out, opcode[2], opcode[3], not_3_out, not_6_out);
  and u_beq (beq, not_2_out, not_1_out, opcode[2], not_4_out, not_3_out, not_6_out);
  and u_lui (lui, opcode[0], opcode[1], opcode[2], opcode[3], not_3_out, not_6_out);
  and u_j (j, not_2_out, opcode[1], not_5_out, not_4_out, not_3_out, not_6_out);
  and u_jal (jal, opcode[0], opcode[1], not_5_out, not_4_out, not_3_out, not_6_out);
  and u_jr (jr, not_2_out, not_1_out, not_5_out, not_4_out, not_3_out, not_6_out, not_8_out, not_10_out, not_9_out, func[3], not_12_out, not_11_out);
  and u_jalr (jalr, not_2_out, not_1_out, not_5_out, not_4_out, not_3_out, not_6_out, func[0], not_10_out, not_9_out, func[3], not_12_out, not_11_out);
  buf or_1 (ifbeq, beq);  // OR_Gate
  buf or_2 (memwrite, sw);  // OR_Gate
  buf or_3 (mentoreg, lw);  // OR_Gate
  or or_4 (alusrc, lw, sw, lui, aluop[1]);
  or or_5 (regdst, jalr, aluop[0], addu);
  or or_6 (we, lw, aluop[0], addu, aluop[1], lui, jal, jalr);
  not not_13 (extop, lui);
  or or_7 (ifj, j, jal);
  buf or_8 (ifjal_writeaddress, jal);  // OR_Gate
  or or_9 (ifjr, jr, jalr);
  or or_10 (ifjal_writedata, jal, jalr);

  // Other names for the same wires on the sheet: subu = aluop[0]; ori = aluop[1]; f0 = func[0]; f1 = func[1];
  //   f2 = func[2]; f3 = func[3]; f4 = func[4]; f5 = func[5]; op0 = opcode[0]; op1 = opcode[1]; op2 = opcode[2];
  //   op3 = opcode[3]; op4 = opcode[4]; op5 = opcode[5]
endmodule

// ifu
module IFU (
  input  ifbeq,
  input  zero,
  input  ifj,
  input  ifjr,
  input  [31:0] jr_rs,
  input  clk,
  input  reset,
  output [31:0] instr,
  output [31:0] pc_4
);

  wire and_1_out, and_2_out, and_3_out, and_4_out, not_1_out, not_2_out, not_3_out, not_4_out, not_5_out,
       not_6_out, not_7_out, not_8_out;
  wire [1:0] sel;
  wire [31:0] beq_pc, bit_extender_1_out, multiplexer_1_out, pc, shifter_1_out;

  not not_1 (not_1_out, ifjr);
  not not_2 (not_2_out, ifbeq);
  not not_3 (not_3_out, ifjr);
  not not_4 (not_4_out, ifj);
  Multiplexer #(.select(2), .width(32)) multiplexer_1 (
    .in0(pc_4), .in1(jr_rs), .in2({pc[31:28], instr[25:0], 2'b00}), .in3(beq_pc), .out(multiplexer_1_out),
    .sel(sel));  // open: en
  Adder #(.width(32)) adder_1 (.a(pc), .b(32'h4), .out(pc_4));  // open: cin, cout
  assign bit_extender_1_out = {{16{instr[15]}}, instr[15:0]};  // Bit_Extender bit_extender_1
  and and_1 (and_1_out, not_1_out, not_2_out, ifj);
  and and_2 (and_2_out, not_3_out, not_4_out, ifbeq, zero);
  Register #(.width(32)) u_PC (.D(multiplexer_1_out), .Q(pc), .clk(clk), .clr(reset));  // open: en
  Shifter #(.width(32)) shifter_1 (.in(bit_extender_1_out), .\dist (5'b00010), .out(shifter_1_out));
  or or_1 (sel[1], and_1_out, and_2_out);
  Adder #(.width(32)) adder_2 (.a(shifter_1_out), .b(pc_4), .out(beq_pc));  // open: cin, cout
  not not_5 (not_5_out, ifj);
  not not_6 (not_6_out, ifbeq);
  not not_7 (not_7_out, ifjr);
  not not_8 (not_8_out, ifj);
  and and_3 (and_3_out, not_5_out, not_6_out, ifjr);
  and and_4 (and_4_out, not_7_out, not_8_out, ifbeq, zero);
  ROM #(.addrWidth(5), .dataWidth(32)) rom_1 (.addr(pc[6:2]), .data(instr));  // open: sel
  or or_2 (sel[0], and_3_out, and_4_out);

  // Other names for the same wires on the sheet: inst[31:0] = instr; imm28[27:2] = instr[25:0];
  //   pc_j[31:2] = {pc[31:28], instr[25:0]}

  // Notes on the sheet:
  //   contents of rom_1 (hex, n*v repeats v):
  //   430821 c000c03 220823 8e610000 8e620004 3e01809
endmodule

// ext
module EXT (
  input  [15:0] in_1,
  input  extop,
  output [31:0] out_3
);

  wire [31:0] bit_extender_1_out;

  assign bit_extender_1_out = {{16{1'b0}}, in_1};  // Bit_Extender bit_extender_1
  Multiplexer #(.width(32)) multiplexer_1 (
    .in0({in_1, {16{1'b0}}}), .in1(bit_extender_1_out), .out(out_3), .sel(extop));  // open: en
endmodule
