// Logisim project CPU_P4.circ as structural Verilog: 7 circuits, main circuit main
module main (
  input  reset,
  output [31:0] out_2,
  output out_3,
  output [4:0] out_4,
  output [31:0] out_5,
  output out_6,
  output [4:0] out_7,
  output [31:0] out_8
);

  wire ALUSrc, clk_2_out, clk_3_out, clk_out, IfZero, Jal, Jr, Jump, MemtoReg, nPC_sel, RegDst;
  wire [1:0] ExtOp_1_0;
  wire [3:0] ALUctr_1_0;
  wire [4:0] multiplexer_1_out;
  wire [31:0] ALUOutput_C, dm_1_out_8, multiplexer_3_out, multiplexer_4_out, out32, PC_and_4, ra_addr;
  wire [31:5] divider_1_out;

  Clock clk (.out(clk_out));
  IFU ifu_1 (
    .nPC_sel(nPC_sel), .IfZero(IfZero), .reset(reset), .Instr(out_2), .clk(clk_out), .Jump(Jump),
    .ra_addr(ra_addr), .Jr(Jr), .PC_and_4(PC_and_4));
  Multiplexer #(.width(5)) multiplexer_1 (
    .in0(out_2[20:16]), .in1(out_2[15:11]), .out(multiplexer_1_out), .sel(RegDst));  // open: en
  Multiplexer #(.width(5)) multiplexer_2 (
    .in0(multiplexer_1_out), .in1({5{1'b1}}), .out(out_4), .sel(Jal));  // open: en
  Clock clk_2 (.out(clk_2_out));
  EXT ext_1 (.imm16(out_2[15:0]), .out32(out32), .EXTOp(ExtOp_1_0));
  GRF grf_1 (
    .in_4(out_2[25:21]), .in_5(out_2[20:16]), .in_6(out_4), .in_7(out_5), .out_8(ra_addr), .out_9(out_8),
    .in_1(clk_2_out), .in_3(out_3), .in_2(reset));
  Controller controller_1 (
    .OpCode(out_2[31:26]), .Func(out_2[5:0]), .RegDst(RegDst), .ALUSrc(ALUSrc), .MemtoReg(MemtoReg),
    .RegWrite(out_3), .ALUctr_1_0(ALUctr_1_0), .nPC_sel(nPC_sel), .ExtOp_1_0(ExtOp_1_0), .MemWrite(out_6),
    .Jump(Jump), .Jal(Jal), .Jr(Jr));
  Clock clk_3 (.out(clk_3_out));
  Multiplexer #(.width(32)) multiplexer_3 (
    .in0(out_8), .in1(out32), .out(multiplexer_3_out), .sel(ALUSrc));  // open: en
  DM dm_1 (.A(ALUOutput_C), .B(out_8), .out_8(dm_1_out_8), .str(out_6), .CLK(clk_3_out), .clr(reset));  // open: sel, ld
  ALU alu_1 (.A(ra_addr), .B(multiplexer_3_out), .C(ALUOutput_C), .ALUctr(ALUctr_1_0), .IfZero(IfZero));
  Multiplexer #(.width(32)) multiplexer_4 (
    .in0(ALUOutput_C), .in1(dm_1_out_8), .out(multiplexer_4_out), .sel(MemtoReg));  // open: en
  Multiplexer #(.width(32)) multiplexer_5 (
    .in0(multiplexer_4_out), .in1(PC_and_4), .out(out_5), .sel(Jal));  // open: en
  Divider #(.width(32)) divider_1 (.a(ALUOutput_C), .b(32'h4), .out({divider_1_out, out_7}));  // open: upper, rem

  // Other names for the same wires on the sheet: MemAddr[4:0] = out_7; func[5:0] = out_2[5:0];
  //   imm16[15:0] = out_2[15:0]; Instr[31:0] = out_2; rd[4:0] = out_2[15:11]; MemWrite = out_6;
  //   opcode[5:0] = out_2[31:26]; RegData1[31:0] = ra_addr; RegAddr[4:0] = out_4; RegData[31:0] = out_5;
  //   MemData[31:0] = out_8; RegData2[31:0] = out_8; RegWrite = out_3; rs[4:0] = out_2[25:21]; rt[4:0] = out_2[20:16]
endmodule

module GRF (
  input  in_1,
  input  in_2,
  input  in_3,
  input  [4:0] in_4,
  input  [4:0] in_5,
  input  [4:0] in_6,
  input  [31:0] in_7,
  output [31:0] out_8,
  output [31:0] out_9
);

  wire WE0, WE1, WE2, WE3, WE4, WE5, WE6, WE7, WE8, WE9, WE10, WE11, WE12, WE13, WE14, WE15, WE16, WE17,
       WE18, WE19, WE20, WE21, WE22, WE23, WE24, WE25, WE26, WE27, WE28, WE29, WE30, WE31;
  wire [31:0] _0, _1, _2, _3, _4, _5, _6, _7, _8, _9, _10, _11, _12, _13, _14, _15, _16, _17, _18, _19, _20,
       _21, _22, _23, _24, _25, _26, _27, _28, _29, _30, _31;

  Demultiplexer #(.select(5)) demultiplexer_1 (
    .out0(WE0), .out1(WE1), .out2(WE2), .out3(WE3), .out4(WE4), .out5(WE5), .out6(WE6), .out7(WE7),
    .out8(WE8), .out9(WE9), .out10(WE10), .out11(WE11), .out12(WE12), .out13(WE13), .out14(WE14),
    .out15(WE15), .out16(WE16), .out17(WE17), .out18(WE18), .out19(WE19), .out20(WE20), .out21(WE21),
    .out22(WE22), .out23(WE23), .out24(WE24), .out25(WE25), .out26(WE26), .out27(WE27), .out28(WE28),
    .out29(WE29), .out30(WE30), .out31(WE31), .in(in_3), .sel(in_6));  // open: en
  Register #(.width(32)) register_1 (.D({32{1'b0}}), .en(WE0), .Q(_0), .clk(in_1), .clr(in_2));
  Register #(.width(32)) register_2 (.D(in_7), .en(WE4), .Q(_4), .clk(in_1), .clr(in_2));
  Register #(.width(32)) register_3 (.D(in_7), .en(WE8), .Q(_8), .clk(in_1), .clr(in_2));
  Register #(.width(32)) register_4 (.D(in_7), .en(WE12), .Q(_12), .clk(in_1), .clr(in_2));
  Register #(.width(32)) register_5 (.D(in_7), .en(WE16), .Q(_16), .clk(in_1), .clr(in_2));
  Register #(.width(32)) register_6 (.D(in_7), .en(WE20), .Q(_20), .clk(in_1), .clr(in_2));
  Register #(.width(32)) register_7 (.D(in_7), .en(WE24), .Q(_24), .clk(in_1), .clr(in_2));
  Register #(.width(32)) register_8 (.D(in_7), .en(WE28), .Q(_28), .clk(in_1), .clr(in_2));
  Register #(.width(32)) register_9 (.D(in_7), .en(WE1), .Q(_1), .clk(in_1), .clr(in_2));
  Register #(.width(32)) register_10 (.D(in_7), .en(WE5), .Q(_5), .clk(in_1), .clr(in_2));
  Register #(.width(32)) register_11 (.D(in_7), .en(WE9), .Q(_9), .clk(in_1), .clr(in_2));
  Register #(.width(32)) register_12 (.D(in_7), .en(WE13), .Q(_13), .clk(in_1), .clr(in_2));
  Register #(.width(32)) register_13 (.D(in_7), .en(WE17), .Q(_17), .clk(in_1), .clr(in_2));
  Register #(.width(32)) register_14 (.D(in_7), .en(WE21), .Q(_21), .clk(in_1), .clr(in_2));
  Register #(.width(32)) register_15 (.D(in_7), .en(WE25), .Q(_25), .clk(in_1), .clr(in_2));
  Register #(.width(32)) register_16 (.D(in_7), .en(WE29), .Q(_29), .clk(in_1), .clr(in_2));
  Register #(.width(32)) register_17 (.D(in_7), .en(WE2), .Q(_2), .clk(in_1), .clr(in_2));
  Register #(.width(32)) register_18 (.D(in_7), .en(WE6), .Q(_6), .clk(in_1), .clr(in_2));
  Register #(.width(32)) register_19 (.D(in_7), .en(WE10), .Q(_10), .clk(in_1), .clr(in_2));
  Register #(.width(32)) register_20 (.D(in_7), .en(WE14), .Q(_14), .clk(in_1), .clr(in_2));
  Register #(.width(32)) register_21 (.D(in_7), .en(WE18), .Q(_18), .clk(in_1), .clr(in_2));
  Register #(.width(32)) register_22 (.D(in_7), .en(WE22), .Q(_22), .clk(in_1), .clr(in_2));
  Register #(.width(32)) register_23 (.D(in_7), .en(WE26), .Q(_26), .clk(in_1), .clr(in_2));
  Register #(.width(32)) register_24 (.D(in_7), .en(WE30), .Q(_30), .clk(in_1), .clr(in_2));
  Multiplexer #(.select(5), .width(32)) multiplexer_1 (
    .in0(_0), .in1(_1), .in2(_2), .in3(_3), .in4(_4), .in5(_5), .in6(_6), .in7(_7), .in8(_8), .in9(_9),
    .in10(_10), .in11(_11), .in12(_12), .in13(_13), .in14(_14), .in15(_15), .in16(_16), .in17(_17),
    .in18(_18), .in19(_19), .in20(_20), .in21(_21), .in22(_22), .in23(_23), .in24(_24), .in25(_25),
    .in26(_26), .in27(_27), .in28(_28), .in29(_29), .in30(_30), .in31(_31), .out(out_8), .sel(in_4));  // open: en
  Register #(.width(32)) register_25 (.D(in_7), .en(WE3), .Q(_3), .clk(in_1), .clr(in_2));
  Register #(.width(32)) register_26 (.D(in_7), .en(WE7), .Q(_7), .clk(in_1), .clr(in_2));
  Register #(.width(32)) register_27 (.D(in_7), .en(WE11), .Q(_11), .clk(in_1), .clr(in_2));
  Register #(.width(32)) register_28 (.D(in_7), .en(WE15), .Q(_15), .clk(in_1), .clr(in_2));
  Register #(.width(32)) register_29 (.D(in_7), .en(WE19), .Q(_19), .clk(in_1), .clr(in_2));
  Register #(.width(32)) register_30 (.D(in_7), .en(WE23), .Q(_23), .clk(in_1), .clr(in_2));
  Register #(.width(32)) register_31 (.D(in_7), .en(WE27), .Q(_27), .clk(in_1), .clr(in_2));
  Register #(.width(32)) register_32 (.D(in_7), .en(WE31), .Q(_31), .clk(in_1), .clr(in_2));
  Multiplexer #(.select(5), .width(32)) multiplexer_2 (
    .in0(_0), .in1(_1), .in2(_2), .in3(_3), .in4(_4), .in5(_5), .in6(_6), .in7(_7), .in8(_8), .in9(_9),
    .in10(_10), .in11(_11), .in12(_12), .in13(_13), .in14(_14), .in15(_15), .in16(_16), .in17(_17),
    .in18(_18), .in19(_19), .in20(_20), .in21(_21), .in22(_22), .in23(_23), .in24(_24), .in25(_25),
    .in26(_26), .in27(_27), .in28(_28), .in29(_29), .in30(_30), .in31(_31), .out(out_9), .sel(in_5));  // open: en

  // Other names for the same wires on the sheet: clk = in_1; rd[4:0] = in_6; RD1[31:0] = out_8; RD2[31:0] = out_9;
  //   reset = in_2; rs[4:0] = in_4; rt[4:0] = in_5; WD[31:0] = in_7; WE = in_3
endmodule

module ALU (
  input  [3:0] ALUctr,
  input  [31:0] A,
  input  [31:0] B,
  output [31:0] C,
  output IfZero
);

  wire [31:0] ADD, OR, SUB;

  Adder #(.width(32)) adder_1 (.a(A), .b(B), .out(ADD));  // open: cin, cout
  Subtractor #(.width(32)) subtractor_1 (.a(A), .b(B), .out(SUB));  // open: bin, bout
  assign OR = A | B;  // OR_Gate or_1, 32 bits wide
  Multiplexer #(.select(4), .width(32)) multiplexer_1 (
    .in0(ADD), .in1(SUB), .in2(OR), .out(C), .sel(ALUctr));  // open: in3, in4, in5, in6, in7, in8, in9, in10, in11, in12, in13, in14, in15, en
  Comparator #(.width(32), .mode("unsigned")) comparator_1 (.a(SUB), .b({32{1'b0}}), .eq(IfZero));  // open: gt, lt

  // Other names for the same wires on the sheet: F[3:0] = ALUctr
endmodule

module IFU (
  input  [31:0] ra_addr,
  input  Jr,
  input  Jump,
  input  nPC_sel,
  input  IfZero,
  input  reset,
  input  clk,
  output [31:0] Instr,
  output [31:0] PC_and_4
);

  wire branch;
  wire [31:0] bit_extender_1_out, divider_1_out, multiplexer_1_out, multiplexer_2_out, multiplexer_3_out, PC,
       PC_and_4_shamft, shifter_1_out;

  Multiplexer #(.width(32)) multiplexer_1 (
    .in0(PC_and_4), .in1(PC_and_4_shamft), .out(multiplexer_1_out), .sel(branch));  // open: en
  and and_1 (branch, nPC_sel, IfZero);
  Multiplexer #(.width(32)) multiplexer_2 (
    .in0(multiplexer_1_out), .in1({PC_and_4[31:28], Instr[25:0], 2'b00}), .out(multiplexer_2_out), .sel(Jump));  // open: en
  Multiplexer #(.width(32)) multiplexer_3 (
    .in0(multiplexer_2_out), .in1(ra_addr), .out(multiplexer_3_out), .sel(Jr));  // open: en
  assign bit_extender_1_out = {{16{Instr[15]}}, Instr[15:0]};  // Bit_Extender bit_extender_1
  Register #(.width(32)) u_PC (.D(multiplexer_3_out), .Q(PC), .clk(clk), .clr(reset));  // open: en
  Shifter #(.width(32)) shifter_1 (.in(bit_extender_1_out), .\dist (5'b00010), .out(shifter_1_out));
  Adder #(.width(32)) adder_1 (.a(PC_and_4), .b(shifter_1_out), .out(PC_and_4_shamft));  // open: cin, cout
  Divider #(.width(32)) divider_1 (.a(PC), .b(32'h4), .out(divider_1_out));  // open: upper, rem
  Adder #(.width(32)) adder_2 (.a(32'h4), .b(PC), .out(PC_and_4));  // open: cin, cout
  ROM #(.addrWidth(5), .dataWidth(32)) rom_1 (.addr(divider_1_out[4:0]), .data(Instr));  // open: sel

  // Other names for the same wires on the sheet: Instr_index[25:0] = Instr[25:0];
  //   Jump_index[31:2] = {PC_and_4[31:28], Instr[25:0]}; shamft[15:0] = Instr[15:0]

  // Notes on the sheet:
  //   理论上如果寻址是四字节，但是这是按字寻址，所以不用加四或者左移两位,ROM要ctrl+R才能用
  //   contents of rom_1 (hex, n*v repeats v):
  //   34090010 34080000 340a0001 34110004 3c10ffff ae300000 11090008 0 c000c0b 10a4021 8000c06 8e300000
  //   2098023 ae300000 3e00008 ae290008
endmodule

module DM (
  input  [31:0] A,
  input  [31:0] B,
  input  str,
  input  sel,
  input  CLK,
  input  ld,
  input  clr,
  output [31:0] out_8
);

  RAM #(.addrWidth(5), .dataWidth(32), .bus("separate")) ram_1 (
    .addr(A[6:2]), .din(B), .data(out_8), .str(str), .sel(sel), .clk(CLK), .ld(ld), .clr(clr));

  // Other names for the same wires on the sheet: C[31:0] = out_8

  // Notes on the sheet:
  //   输出的也是LOGISIM里面的地址，所以使用时要除以4，输出也要除以4
endmodule

module Controller (
  input  [5:0] OpCode,
  input  [5:0] Func,
  output Jr,
  output Jal,
  output Jump,
  output RegDst,
  output nPC_sel,
  output [1:0] ExtOp_1_0,
  output MemtoReg,
  output [3:0] ALUctr_1_0,
  output MemWrite,
  output ALUSrc,
  output RegWrite
);

  wire addu, beq, j, jal_t, jr_t, lui, lw, not_1_out, not_2_out, not_3_out, not_4_out, not_5_out, not_6_out,
       not_7_out, not_8_out, not_9_out, not_10_out, not_11_out, not_12_out, not_13_out, not_14_out,
       not_15_out, not_16_out, not_17_out, not_18_out, not_19_out, not_20_out, not_21_out, not_22_out,
       not_23_out, not_24_out, not_25_out, not_26_out, not_27_out, not_28_out, not_29_out, not_30_out,
       not_31_out, not_32_out, not_33_out, not_34_out, not_35_out, not_36_out, not_37_out, not_38_out,
       not_39_out, not_40_out, not_41_out, not_42_out, not_43_out, not_44_out, not_45_out, not_46_out,
       not_47_out, not_48_out, not_49_out, not_50_out, not_51_out, not_52_out, not_53_out, not_54_out, ori,
       subu, sw;

  buf or_1 (Jr, jr_t);  // OR_Gate
  or or_2 (RegDst, addu, subu);
  buf or_3 (MemWrite, sw);  // OR_Gate
  not not_1 (not_1_out, OpCode[0]);
  not not_2 (not_2_out, OpCode[1]);
  not not_3 (not_3_out, OpCode[2]);
  not not_4 (not_4_out, OpCode[3]);
  not not_5 (not_5_out, OpCode[4]);
  not not_6 (not_6_out, OpCode[5]);
  not not_7 (not_7_out, Func[1]);
  not not_8 (not_8_out, Func[2]);
  not not_9 (not_9_out, Func[3]);
  not not_10 (not_10_out, Func[4]);
  not not_11 (not_11_out, OpCode[2]);
  not not_12 (not_12_out, OpCode[4]);
  not not_13 (not_13_out, OpCode[0]);
  not not_14 (not_14_out, OpCode[1]);
  not not_15 (not_15_out, OpCode[3]);
  not not_16 (not_16_out, OpCode[4]);
  not not_17 (not_17_out, OpCode[5]);
  not not_18 (not_18_out, OpCode[0]);
  not not_19 (not_19_out, OpCode[2]);
  not not_20 (not_20_out, OpCode[3]);
  not not_21 (not_21_out, OpCode[4]);
  not not_22 (not_22_out, OpCode[5]);
  and and_1 (addu, not_1_out, not_2_out, not_3_out, not_4_out, not_5_out, not_6_out, Func[0], not_7_out, not_8_out, not_9_out, not_10_out, Func[5]);
  and and_2 (sw, OpCode[0], OpCode[1], not_11_out, OpCode[3], not_12_out, OpCode[5]);
  and and_3 (beq, not_13_out, not_14_out, OpCode[2], not_15_out, not_16_out, not_17_out);
  and and_4 (j, not_18_out, OpCode[1], not_19_out, not_20_out, not_21_out, not_22_out);
  buf or_4 (Jal, jal_t);  // OR_Gate
  buf or_5 (nPC_sel, beq);  // OR_Gate
  or or_6 (ALUSrc, ori, lw, lui, sw);
  not not_23 (not_23_out, OpCode[0]);
  not not_24 (not_24_out, OpCode[1]);
  not not_25 (not_25_out, OpCode[2]);
  not not_26 (not_26_out, OpCode[3]);
  not not_27 (not_27_out, OpCode[4]);
  not not_28 (not_28_out, OpCode[5]);
  not not_29 (not_29_out, Func[2]);
  not not_30 (not_30_out, Func[3]);
  not not_31 (not_31_out, Func[4]);
  not not_32 (not_32_out, OpCode[1]);
  not not_33 (not_33_out, OpCode[4]);
  not not_34 (not_34_out, OpCode[5]);
  not not_35 (not_35_out, OpCode[2]);
  not not_36 (not_36_out, OpCode[3]);
  not not_37 (not_37_out, OpCode[4]);
  and and_5 (subu, not_23_out, not_24_out, not_25_out, not_26_out, not_27_out, not_28_out, Func[0], Func[1], not_29_out, not_30_out, not_31_out, Func[5]);
  and and_6 (ori, OpCode[0], not_32_out, OpCode[2], OpCode[3], not_33_out, not_34_out);
  and and_7 (lw, OpCode[0], OpCode[1], not_35_out, not_36_out, not_37_out, OpCode[5]);
  or or_7 (Jump, j, jal_t);
  buf or_8 (MemtoReg, lw);  // OR_Gate
  or or_9 (RegWrite, addu, subu, lui, ori, lw, jal_t);
  not not_38 (not_38_out, OpCode[0]);
  not not_39 (not_39_out, OpCode[1]);
  not not_40 (not_40_out, OpCode[2]);
  not not_41 (not_41_out, OpCode[3]);
  not not_42 (not_42_out, OpCode[4]);
  not not_43 (not_43_out, OpCode[5]);
  not not_44 (not_44_out, OpCode[2]);
  not not_45 (not_45_out, OpCode[3]);
  not not_46 (not_46_out, OpCode[4]);
  not not_47 (not_47_out, OpCode[5]);
  not not_48 (not_48_out, OpCode[4]);
  not not_49 (not_49_out, OpCode[5]);
  or or_10 (ExtOp_1_0[0], lw, sw);
  buf or_11 (ExtOp_1_0[1], lui);  // OR_Gate
  buf or_12 (ALUctr_1_0[0], subu);  // OR_Gate
  buf or_13 (ALUctr_1_0[1], ori);  // OR_Gate
  and and_8 (jr_t, not_38_out, not_39_out, not_40_out, not_41_out, not_42_out, not_43_out, not_50_out, not_51_out, not_52_out, Func[3], not_53_out, not_54_out);
  not not_50 (not_50_out, Func[0]);
  not not_51 (not_51_out, Func[1]);
  not not_52 (not_52_out, Func[2]);
  not not_53 (not_53_out, Func[4]);
  not not_54 (not_54_out, Func[5]);
  and and_9 (jal_t, OpCode[0], OpCode[1], not_44_out, not_45_out, not_46_out, not_47_out);
  and and_10 (lui, OpCode[0], OpCode[1], OpCode[2], OpCode[3], not_48_out, not_49_out);

  assign ALUctr_1_0[3:2] = 2'b00;

  // Other names for the same wires on the sheet: ALUctr[1:0] = ALUctr_1_0[1:0]; ALUctr0 = ALUctr_1_0[0];
  //   ALUctr1 = ALUctr_1_0[1]; ExtOp[1:0] = ExtOp_1_0; ExtOp0 = ExtOp_1_0[0]; ExtOp1 = ExtOp_1_0[1]; op0 = OpCode[0];
  //   op1 = OpCode[1]; op2 = OpCode[2]; op3 = OpCode[3]; op4 = OpCode[4]; op5 = OpCode[5]
endmodule

module EXT (
  input  [1:0] EXTOp,
  input  [15:0] imm16,
  output [31:0] out32
);

  wire [31:0] sign_ext, zero_ext;

  assign zero_ext = {{16{1'b0}}, imm16};  // Bit_Extender bit_extender_1
  assign sign_ext = {{16{imm16[15]}}, imm16};  // Bit_Extender bit_extender_2
  Multiplexer #(.select(2), .width(32)) multiplexer_1 (
    .in0(zero_ext), .in1(sign_ext), .in2({imm16, {16{1'b0}}}), .out(out32), .sel(EXTOp));  // open: in3, en

  // Other names for the same wires on the sheet: lui_ext[31:16] = imm16
endmodule
